# Fritzing sketch DiscoFloor (saved by Fritzing 0.9.1b)
breadboards: 1

parts:
  U1 = MAX485 [part_number=ISL8487E package=dil08]
  LED1 = RGB LED (com. cathode, rgb) [package="5 mm [THT]"]
  IC1 = MICROCONTROLLER [part_number=Atmega168 package=dil28-3-zif_socket]
  R1 = Resistor [tolerance=±5% resistance=220 package=THT]
  R3 = Resistor [tolerance=±5% resistance=220 package=THT]
  R4 = Resistor [tolerance=±5% resistance=220 package=THT]
  R5 = Resistor [tolerance=±5% resistance=220 package=THT]
  XTAL1 = Crystal [frequency="16 Mhz" package=THT]
  C4 = Capacitor [package=cap-pth-small2]
  C3 = Capacitor [package=cap-pth-small2]

nets:
  N1: U1.RO, IC1.PD0(RXD)
  N2: U1.RE, U1.DE, IC1.PD2(INT0)
  N3: U1.DI, IC1.PD1(TXD)
  GND: U1.GND, LED1.common_cathode, IC1.GND, C4.2, C3.2
  To Bus: U1.A, U1.B
  5V: U1.VCC, IC1.VCC
  N4: LED1.red_anode, R4.Pin_1
  N5: LED1.green_anode, R3.Pin_1
  N6: LED1.blue_anode, R5.Pin_1
  N7: IC1.PD3(INT1), R1.Pin_0
  Cap Sensor: IC1.PD4(XCK_T0), R1.Pin_1
  N8: IC1.PB6(XTAL1_TOSC1), XTAL1.pin_1, C3.1
  N9: IC1.PB7(XTAL2_TOSC2), XTAL1.pin_0, C4.1
  Next node: IC1.PD5(T1)
  Previous node: IC1.PD6(AIN0)
  N10: IC1.PB1(OC1A), R5.Pin_0
  N11: IC1.PB2(SS_OC1B), R3.Pin_0
  N12: IC1.PB3(MOSI_OC2), R4.Pin_0

notes:
  Capacitive Sensor Area
  To next node
  To previous node
  To RS485 Bus
